# Fritzing sketch Circuit diagram (saved by Fritzing 0.9.3b)

parts:
  A1 = Esp32-c3 super mini
  TP1 = TP4056 [chip_label=TP4056 package="DIP (Dual Inline) [THT]"]
  BAT1 = Battery Holders [package=lipo-1100mAh]
  Bauteil1 = AHT20 BMP280 pressure and humidity breakout
  Mod1 = ossoyoo-lora-module
  A2 = u-blox NEO-6M GPS Breakout
  R2 = Resistor [tolerance=±1% resistance=10k package=THT]
  S1 = Toggle Switch [package=THT]
  R3 = Resistor [tolerance=±5% resistance=10k package=THT]
  A3 = Esp32-c3 super mini
  Mod2 = ossoyoo-lora-module
  A4 = u-blox NEO-6M GPS Breakout

nets:
  N1: A1.Pin_1, A2.Pin_4
  N2: A1.Pin_2, Mod1.M0
  N3: A1.Pin_3, Mod1.M1
  N4: A1.Pin_4, Bauteil1.SDA
  N5: A1.Pin_5, Bauteil1.SCL
  N6: A1.Pin_6, Mod1.AUX
  N7: A1.Pin_7, A1.Pin_10, Mod1.TXD
  N8: A1.Pin_8, Mod1.RXD
  N9: A1.Pin_9, R2.Pin_1, R3.Pin_1
  N10: A1.Pin_13, A2.Pin_3
  VDD: A1.Pin_14, Bauteil1.VDD, Mod1.VCC, A2.Pin_1
  GND: A1.Pin_15, TP1.pin6, Bauteil1.GND, Mod1.GND, A2.Pin_2, R2.Pin_0
  N11: A1.Pin_16, S1.L2, R3.Pin_0
  N12: TP1.pin3, S1.COM
  N13: TP1.pin4, BAT1.+
  N14: TP1.pin5, BAT1.-
  N15: A3.Pin_1, A4.Pin_4
  N16: A3.Pin_2, Mod2.M0
  N17: A3.Pin_3, Mod2.M1
  N18: A3.Pin_6, Mod2.AUX
  N19: A3.Pin_7, Mod2.TXD
  N20: A3.Pin_8, Mod2.RXD
  N21: A3.Pin_13, A4.Pin_3
  N22: A3.Pin_14, Mod2.VCC, A4.Pin_1
  N23: A3.Pin_15, Mod2.GND, A4.Pin_2

custom parts:
  Esp32-c3 super mini: ESP32-C3 Development Board ESP32 SuperMini Development Board ESP32 Development Board WiFi Bluetooth.
  TP4056: A DIP stand-in part for whatever IC you want. With 6 pins on a 300mil dual inline package (DIP) footprint.
  AHT20 BMP280 pressure and humidity breakout: Cheap breakout board for the BMP280, barometric pressure sensor, and AHT20, humidity sensor
  ossoyoo-lora-module: Osoyoo Long Distance wireless transceiver Uart LoRa Module.
